// Logisim project Pipeline .circ as structural Verilog: 14 circuits, main circuit main
module main (
  output [1:0] out_1,
  output [1:0] out_2
);

  wire ALUSrc, BEQ, BGEZ, BGT, BGTZ, BLEZ, BLT, BLTZ, BNE, CLK, ex_mem_1_out_18, ExtOp, F_LUI,
       id_ex_1_out_33, id_ex_1_out_35, id_ex_1_out_36, J, JR, Kill1, Kill2, mem_wb_1_out_9, MemRead,
       MemWrite, not_1_out, not_2_out, or_1_out, pull_resistor_1_node, STALL, Zero;
  wire [1:0] id_ex_1_out_34, main_control_unit_1_memtoreg, main_control_unit_1_regdest, MemToReg,
       pc_controller_1_pc_controller, RegDest;
  wire [2:0] ex_mem_1_out_17, Funct, id_ex_1_out_32, mem_wb_1_out_8, multiplexer_3_out, RS, Rt;
  wire [3:0] Opcode;
  wire [5:3] if_id_1_out_7;
  wire [7:0] ALUOP, main_control_unit_1_aluop;
  wire [11:0] adder_1_out, adder_2_out, ex_mem_1_out_13, id_ex_1_out_26, id_ex_1_out_27, id_ex_1_out_28,
       if_id_1_out_6, multiplexer_1_out, multiplexer_4_out, register_1_q;
  wire [15:0] ALUOUT, ex_mem_1_out_14, ex_mem_1_out_15, ex_mem_1_out_16, extender_1_out, id_ex_1_out_29,
       id_ex_1_out_30, id_ex_1_out_31, mem_wb_1_out_7, multiplexer_2_out, multiplexer_7_out,
       multiplexer_8_out, multiplexer_9_out, ram_2_data, RD2, register1_1_rd1, register1_1_rd2, rom_1_data,
       shifter_1_out;
  wire [15:12] multiplexer_4_out_2;
  wire [22:0] multiplexer_6_out;
  wire [27:0] main_control_unit_1_lui;

  RAM #(.addrWidth(12), .dataWidth(16)) ram_1 (.ld(pull_resistor_1_node));  // open: addr, data, sel, clk, clr
  Pull_Resistor #(.pull(1)) pull_resistor_1 (.node(pull_resistor_1_node));
  PC_Controller pc_controller_1 (
    .PC_Controller(pc_controller_1_pc_controller), .Jump(J), .BNE(BNE), .BEQ(BEQ), .BGT(BGT), .BLT(BLT),
    .JR(JR), .BGEZ(BGEZ), .BLEZ(BLEZ), .BGTZ(BGTZ), .BLTZ(BLTZ), .ALUOUT(ALUOUT), .Zero(Zero), .Kill2(Kill2),
    .Kill1(Kill1));
  Multiplexer #(.select(2), .width(12)) multiplexer_1 (
    .in0(adder_1_out), .in1(id_ex_1_out_27), .in2({RS, Rt, if_id_1_out_7, Funct}), .in3(multiplexer_4_out),
    .out(multiplexer_1_out), .sel(pc_controller_1_pc_controller));  // open: en
  not not_1 (not_1_out, STALL);
  Register #(.width(12)) register_1 (.D(multiplexer_1_out), .en(not_1_out), .Q(register_1_q), .clk(CLK));  // open: clr
  Clock clock_1 (.out(CLK));
  Adder #(.width(12)) adder_1 (.a(register_1_q), .b(12'h1), .out(adder_1_out));  // open: cin, cout
  ROM #(.addrWidth(12), .dataWidth(16)) rom_1 (.addr(register_1_q), .data(rom_1_data));  // open: sel
  Multiplexer #(.width(16)) multiplexer_2 (
    .in0(rom_1_data), .in1({16{1'b0}}), .out(multiplexer_2_out), .sel(Kill1));  // open: en
  IF_ID if_id_1 (
    .in_1(adder_1_out), .in_2(multiplexer_2_out), .CLk(CLK), .out_6(if_id_1_out_6),
    .out_7({Opcode, RS, Rt, if_id_1_out_7, Funct}), .En(not_2_out), .Clr(1'b0));
  not not_2 (not_2_out, STALL);
  Multiplexer #(.select(2), .width(3)) multiplexer_3 (
    .in0(Rt), .in1(if_id_1_out_7), .in2(3'b111), .in3(3'b001), .out(multiplexer_3_out), .sel(RegDest));  // open: en
  Register1 register1_1 (
    .R1(RS), .R2(Rt), .W1(mem_wb_1_out_7), .RW(mem_wb_1_out_8), .CLK(CLK), .RD1(register1_1_rd1),
    .RD2(register1_1_rd2), .WE(mem_wb_1_out_9));
  Extender extender_1 (.IN({if_id_1_out_7, Funct}), .OUT(extender_1_out), .Extender(ExtOp));
  Main_Control_Unit main_control_unit_1 (
    .ALUOP(main_control_unit_1_aluop), .OP(Opcode), .FUNC(Funct), .RegWrite(main_control_unit_1_lui[1]),
    .RegDest(main_control_unit_1_regdest), .ALUSrc(main_control_unit_1_lui[22]),
    .ExtOP(main_control_unit_1_lui[25]), .MemW(main_control_unit_1_lui[4]),
    .MemR(main_control_unit_1_lui[5]), .MemToReg(main_control_unit_1_memtoreg),
    .JR(main_control_unit_1_lui[26]), .J(main_control_unit_1_lui[27]), .BEQ(main_control_unit_1_lui[6]),
    .BNE(main_control_unit_1_lui[7]), .BLT(main_control_unit_1_lui[8]), .BGT(main_control_unit_1_lui[9]),
    .BLTZ(main_control_unit_1_lui[10]), .BLEZ(main_control_unit_1_lui[11]),
    .BGTZ(main_control_unit_1_lui[12]), .BGEZ(main_control_unit_1_lui[13]), .RD2(RD2),
    .LUI(main_control_unit_1_lui[0]));
  Multiplexer #(.select(2), .width(16)) multiplexer_4 (
    .in0(register1_1_rd1), .in1(multiplexer_8_out), .in2(multiplexer_9_out), .in3(mem_wb_1_out_7),
    .out({multiplexer_4_out_2, multiplexer_4_out}), .sel(out_1));  // open: en
  Multiplexer #(.select(2), .width(16)) multiplexer_5 (
    .in0(register1_1_rd2), .in1(multiplexer_8_out), .in2(multiplexer_9_out), .in3(mem_wb_1_out_7), .out(RD2),
    .sel(out_2));  // open: en
  Multiplexer #(.width(28)) multiplexer_6 (
    .in0({main_control_unit_1_lui[27:25], main_control_unit_1_regdest, main_control_unit_1_lui[22], main_control_unit_1_aluop, main_control_unit_1_lui[13:4], main_control_unit_1_memtoreg, main_control_unit_1_lui[1:0]}),
    .in1({28{1'b0}}), .out({J, JR, ExtOp, RegDest, multiplexer_6_out}), .sel(or_1_out));  // open: en
  or or_1 (or_1_out, STALL, Kill2);
  Hazard_Detect_Forward_and_Stall hazard_detect_forward_and_stall_1 (
    .RegWrite_MEM(ex_mem_1_out_18), .Rd_MEM(ex_mem_1_out_17), .RegWrite_EX(id_ex_1_out_33),
    .Rd_EX(id_ex_1_out_32), .EX_MemRd(id_ex_1_out_36), .Stall(STALL), .RS(RS), .Rt(Rt),
    .RegWrite_Wb(mem_wb_1_out_9), .Rd_Wb(mem_wb_1_out_8), .Forward_A(out_1), .Forward_B(out_2));
  Adder #(.width(12)) adder_2 (.a(if_id_1_out_6), .b(extender_1_out[11:0]), .out(adder_2_out));  // open: cin, cout
  ID_EX id_ex_1 (
    .in_2(adder_2_out), .in_4({multiplexer_4_out_2, multiplexer_4_out}), .in_5(RD2), .in_6(extender_1_out),
    .in_7(multiplexer_3_out), .out_27(id_ex_1_out_27), .out_29(id_ex_1_out_29), .out_30(id_ex_1_out_30),
    .out_31(id_ex_1_out_31), .out_32(id_ex_1_out_32), .CLK(CLK), .En(1'b1), .Clr(1'b0),
    .in_11(multiplexer_6_out[1]), .out_33(id_ex_1_out_33), .in_12(multiplexer_6_out[3:2]),
    .in_13(multiplexer_6_out[4]), .in_14(multiplexer_6_out[5]), .in_25(multiplexer_6_out[22]),
    .out_35(id_ex_1_out_35), .out_36(id_ex_1_out_36), .out_47(ALUSrc), .out_34(id_ex_1_out_34),
    .out_46(ALUOP), .in_1(if_id_1_out_6), .out_26(id_ex_1_out_26), .in_24(multiplexer_6_out[21:14]),
    .in_16(multiplexer_6_out[6]), .out_38(BEQ), .in_17(multiplexer_6_out[7]), .out_39(BNE),
    .in_18(multiplexer_6_out[8]), .out_40(BLT), .in_19(multiplexer_6_out[9]), .out_41(BGT),
    .in_20(multiplexer_6_out[10]), .out_42(BLTZ), .in_21(multiplexer_6_out[11]), .out_43(BLEZ),
    .in_22(multiplexer_6_out[12]), .out_44(BGTZ), .in_23(multiplexer_6_out[13]), .out_45(BGEZ),
    .in_3({RS, Rt, if_id_1_out_7, Funct}), .out_28(id_ex_1_out_28), .in_15(multiplexer_6_out[0]),
    .out_37(F_LUI));
  Multiplexer #(.width(16)) multiplexer_7 (
    .in0(id_ex_1_out_30), .in1(id_ex_1_out_31), .out(multiplexer_7_out), .sel(ALUSrc));  // open: en
  Shifter #(.width(16)) shifter_1 (.in({4'b0000, id_ex_1_out_28}), .\dist (4'b0100), .out(shifter_1_out));
  _16_Bit_ALU u_16_bit_alu_1 (
    .IN1(id_ex_1_out_29), .IN2(multiplexer_7_out), .Zero_flag(Zero), .OUT(ALUOUT), .in_3(ALUOP));
  Multiplexer #(.width(16)) multiplexer_8 (
    .in0(ALUOUT), .in1(shifter_1_out), .out(multiplexer_8_out), .sel(F_LUI));  // open: en
  EX_MEM ex_mem_1 (
    .in_3(ALUOUT), .in_4(id_ex_1_out_30), .in_5(id_ex_1_out_32), .out_15(ex_mem_1_out_15),
    .out_16(ex_mem_1_out_16), .out_17(ex_mem_1_out_17), .EN(1'b1), .CLK(CLK), .Clr(1'b0),
    .in_9(id_ex_1_out_33), .out_18(ex_mem_1_out_18), .in_10(id_ex_1_out_34), .out_19(MemToReg),
    .in_11(id_ex_1_out_35), .out_20(MemWrite), .in_12(id_ex_1_out_36), .out_21(MemRead),
    .in_1(id_ex_1_out_26), .out_13(ex_mem_1_out_13), .in_2(shifter_1_out), .out_14(ex_mem_1_out_14));
  RAM #(.addrWidth(12), .dataWidth(16), .bus("separate")) ram_2 (
    .addr(ex_mem_1_out_15[11:0]), .din(ex_mem_1_out_16), .data(ram_2_data), .str(MemWrite), .clk(CLK),
    .ld(MemRead));  // open: sel, clr
  Multiplexer #(.select(2), .width(16)) multiplexer_9 (
    .in0(ex_mem_1_out_15), .in1(ram_2_data), .in2({4'b0000, ex_mem_1_out_13}), .in3(ex_mem_1_out_14),
    .out(multiplexer_9_out), .sel(MemToReg));  // open: en
  MEM_WB mem_wb_1 (
    .in_1(multiplexer_9_out), .in_2(ex_mem_1_out_17), .out_7(mem_wb_1_out_7), .out_8(mem_wb_1_out_8),
    .En(1'b1), .CLK(CLK), .Clr(1'b0), .in_6(ex_mem_1_out_18), .out_9(mem_wb_1_out_9));

  // Other names for the same wires on the sheet: Forward_A[1:0] = out_1; Forward_B[1:0] = out_2

  // Notes on the sheet:
  //   JR
  //   J
  //   Branch
  //   PC+1
  //   contents of rom_1 (hex, n*v repeats v):
  //   a384 8354 35b 2040 2081 20c2 890a 1921 1520 14f2 4c02 1290 403b 3100 b012 55c 1b68 403f 4e9 2040
  //   2285 22c6 4e0 3100 1e06
  //   LUI
endmodule

module Register1 (
  input  [2:0] R1,
  input  [2:0] R2,
  input  [15:0] W1,
  input  [2:0] RW,
  input  WE,
  input  CLK,
  output [15:0] RD1,
  output [15:0] RD2
);

  wire demultiplexer_2_out0, demultiplexer_2_out1, demultiplexer_2_out2, demultiplexer_2_out3,
       demultiplexer_2_out4, demultiplexer_2_out5, demultiplexer_2_out6, demultiplexer_2_out7;
  wire [15:0] demultiplexer_1_out1, demultiplexer_1_out2, demultiplexer_1_out3, demultiplexer_1_out4,
       demultiplexer_1_out5, demultiplexer_1_out6, demultiplexer_1_out7, register_1_q, register_2_q,
       register_3_q, register_4_q, register_5_q, register_6_q, register_7_q, register_8_q;

  Demultiplexer #(.select(3), .width(16)) demultiplexer_1 (
    .out1(demultiplexer_1_out1), .out2(demultiplexer_1_out2), .out3(demultiplexer_1_out3),
    .out4(demultiplexer_1_out4), .out5(demultiplexer_1_out5), .out6(demultiplexer_1_out6),
    .out7(demultiplexer_1_out7), .in(W1), .sel(RW));  // open: out0, en
  Demultiplexer #(.select(3)) demultiplexer_2 (
    .out0(demultiplexer_2_out0), .out1(demultiplexer_2_out1), .out2(demultiplexer_2_out2),
    .out3(demultiplexer_2_out3), .out4(demultiplexer_2_out4), .out5(demultiplexer_2_out5),
    .out6(demultiplexer_2_out6), .out7(demultiplexer_2_out7), .in(WE), .sel(RW));  // open: en
  Register #(.width(16)) register_1 (
    .D({16{1'b0}}), .en(demultiplexer_2_out0), .Q(register_1_q), .clk(CLK));  // open: clr
  Register #(.width(16)) register_2 (
    .D(demultiplexer_1_out1), .en(demultiplexer_2_out1), .Q(register_2_q), .clk(CLK));  // open: clr
  Register #(.width(16)) register_3 (
    .D(demultiplexer_1_out2), .en(demultiplexer_2_out2), .Q(register_3_q), .clk(CLK));  // open: clr
  Register #(.width(16)) register_4 (
    .D(demultiplexer_1_out3), .en(demultiplexer_2_out3), .Q(register_4_q), .clk(CLK));  // open: clr
  Register #(.width(16)) register_5 (
    .D(demultiplexer_1_out4), .en(demultiplexer_2_out4), .Q(register_5_q), .clk(CLK));  // open: clr
  Register #(.width(16)) register_6 (
    .D(demultiplexer_1_out5), .en(demultiplexer_2_out5), .Q(register_6_q), .clk(CLK));  // open: clr
  Register #(.width(16)) register_7 (
    .D(demultiplexer_1_out6), .en(demultiplexer_2_out6), .Q(register_7_q), .clk(CLK));  // open: clr
  Register #(.width(16)) register_8 (
    .D(demultiplexer_1_out7), .en(demultiplexer_2_out7), .Q(register_8_q), .clk(CLK));  // open: clr
  Multiplexer #(.select(3), .width(16)) multiplexer_1 (
    .in0(register_1_q), .in1(register_2_q), .in2(register_3_q), .in3(register_4_q), .in4(register_5_q),
    .in5(register_6_q), .in6(register_7_q), .in7(register_8_q), .out(RD1), .sel(R1));  // open: en
  Multiplexer #(.select(3), .width(16)) multiplexer_2 (
    .in0(register_1_q), .in1(register_2_q), .in2(register_3_q), .in3(register_4_q), .in4(register_5_q),
    .in5(register_6_q), .in6(register_7_q), .in7(register_8_q), .out(RD2), .sel(R2));  // open: en
endmodule

module _1_Bit_ALU (
  input  [2:0] OP,
  input  Sub,
  input  Cin,
  input  IN1,
  input  Less,
  input  LessU,
  input  IN2,
  output OUT,
  output SET,
  output Cout
);

  wire and_1_out, nor_1_out, or_1_out, xor_1_out, xor_2_out;

  xor xor_1 (xor_1_out, IN2, Sub);
  and and_1 (and_1_out, IN1, IN2);
  or or_1 (or_1_out, IN1, IN2);
  xor xor_2 (xor_2_out, IN1, IN2);
  nor nor_1 (nor_1_out, IN1, IN2);
  Adder #(.width(1)) adder_1 (.a(IN1), .b(xor_1_out), .out(SET), .cin(Cin), .cout(Cout));
  Multiplexer #(.select(3)) multiplexer_1 (
    .in0(and_1_out), .in1(or_1_out), .in2(xor_2_out), .in3(nor_1_out), .in4(SET), .in5(Less), .in6(LessU),
    .out(OUT), .sel(OP));  // open: in7, en
endmodule

module _16_Bit_ALU (
  input  [15:0] IN1,
  input  [15:0] IN2,
  input  [7:0] in_3,
  output Zero_flag,
  output [15:0] OUT
);

  wire and_1_out, n1_bit_alu_1_cout, n1_bit_alu_2_cout, n1_bit_alu_3_cout, n1_bit_alu_4_cout,
       n1_bit_alu_5_cout, n1_bit_alu_6_cout, n1_bit_alu_7_cout, n1_bit_alu_8_cout, n1_bit_alu_9_cout,
       n1_bit_alu_10_cout, n1_bit_alu_11_cout, n1_bit_alu_12_cout, n1_bit_alu_13_cout, n1_bit_alu_14_cout,
       n1_bit_alu_15_cout, n1_bit_alu_16_cout, n1_bit_alu_16_set, not_1_out, not_2_out, or_1_out, or_2_out,
       or_3_out;
  wire [15:0] bit_extender_1_out, bit_extender_2_out, bit_extender_3_out, n1_bit_alu_1_out, shifter_1_out,
       shifter_2_out, shifter_3_out, shifter_4_out;

  not not_1 (not_1_out, n1_bit_alu_16_cout);
  _1_Bit_ALU u_1_bit_alu_1 (
    .OP(in_3[2:0]), .IN1(IN1[0]), .Less(n1_bit_alu_16_set), .IN2(IN2[0]), .OUT(n1_bit_alu_1_out[0]),
    .Cout(n1_bit_alu_1_cout), .Sub(in_3[3]), .Cin(in_3[3]), .LessU(not_1_out));  // open: SET
  _1_Bit_ALU u_1_bit_alu_2 (
    .OP(in_3[2:0]), .IN1(IN1[1]), .Less(1'b0), .IN2(IN2[1]), .OUT(n1_bit_alu_1_out[1]),
    .Cout(n1_bit_alu_2_cout), .Sub(in_3[3]), .Cin(n1_bit_alu_1_cout), .LessU(1'b0));  // open: SET
  _1_Bit_ALU u_1_bit_alu_3 (
    .OP(in_3[2:0]), .IN1(IN1[2]), .Less(1'b0), .IN2(IN2[2]), .OUT(n1_bit_alu_1_out[2]),
    .Cout(n1_bit_alu_3_cout), .Sub(in_3[3]), .Cin(n1_bit_alu_2_cout), .LessU(1'b0));  // open: SET
  _1_Bit_ALU u_1_bit_alu_4 (
    .OP(in_3[2:0]), .IN1(IN1[3]), .Less(1'b0), .IN2(IN2[3]), .OUT(n1_bit_alu_1_out[3]),
    .Cout(n1_bit_alu_4_cout), .Sub(in_3[3]), .Cin(n1_bit_alu_3_cout), .LessU(1'b0));  // open: SET
  _1_Bit_ALU u_1_bit_alu_5 (
    .OP(in_3[2:0]), .IN1(IN1[4]), .Less(1'b0), .IN2(IN2[4]), .OUT(n1_bit_alu_1_out[4]),
    .Cout(n1_bit_alu_5_cout), .Sub(in_3[3]), .Cin(n1_bit_alu_4_cout), .LessU(1'b0));  // open: SET
  _1_Bit_ALU u_1_bit_alu_6 (
    .OP(in_3[2:0]), .IN1(IN1[5]), .Less(1'b0), .IN2(IN2[5]), .OUT(n1_bit_alu_1_out[5]),
    .Cout(n1_bit_alu_6_cout), .Sub(in_3[3]), .Cin(n1_bit_alu_5_cout), .LessU(1'b0));  // open: SET
  _1_Bit_ALU u_1_bit_alu_7 (
    .OP(in_3[2:0]), .IN1(IN1[6]), .Less(1'b0), .IN2(IN2[6]), .OUT(n1_bit_alu_1_out[6]),
    .Cout(n1_bit_alu_7_cout), .Sub(in_3[3]), .Cin(n1_bit_alu_6_cout), .LessU(1'b0));  // open: SET
  _1_Bit_ALU u_1_bit_alu_8 (
    .OP(in_3[2:0]), .IN1(IN1[7]), .Less(1'b0), .IN2(IN2[7]), .OUT(n1_bit_alu_1_out[7]),
    .Cout(n1_bit_alu_8_cout), .Sub(in_3[3]), .Cin(n1_bit_alu_7_cout), .LessU(1'b0));  // open: SET
  _1_Bit_ALU u_1_bit_alu_9 (
    .OP(in_3[2:0]), .IN1(IN1[8]), .Less(1'b0), .IN2(IN2[8]), .OUT(n1_bit_alu_1_out[8]),
    .Cout(n1_bit_alu_9_cout), .Sub(in_3[3]), .Cin(n1_bit_alu_8_cout), .LessU(1'b0));  // open: SET
  _1_Bit_ALU u_1_bit_alu_10 (
    .OP(in_3[2:0]), .IN1(IN1[9]), .Less(1'b0), .IN2(IN2[9]), .OUT(n1_bit_alu_1_out[9]),
    .Cout(n1_bit_alu_10_cout), .Sub(in_3[3]), .Cin(n1_bit_alu_9_cout), .LessU(1'b0));  // open: SET
  _1_Bit_ALU u_1_bit_alu_11 (
    .OP(in_3[2:0]), .IN1(IN1[10]), .Less(1'b0), .IN2(IN2[10]), .OUT(n1_bit_alu_1_out[10]),
    .Cout(n1_bit_alu_11_cout), .Sub(in_3[3]), .Cin(n1_bit_alu_10_cout), .LessU(1'b0));  // open: SET
  _1_Bit_ALU u_1_bit_alu_12 (
    .OP(in_3[2:0]), .IN1(IN1[11]), .Less(1'b0), .IN2(IN2[11]), .OUT(n1_bit_alu_1_out[11]),
    .Cout(n1_bit_alu_12_cout), .Sub(in_3[3]), .Cin(n1_bit_alu_11_cout), .LessU(1'b0));  // open: SET
  _1_Bit_ALU u_1_bit_alu_13 (
    .OP(in_3[2:0]), .IN1(IN1[12]), .Less(1'b0), .IN2(IN2[12]), .OUT(n1_bit_alu_1_out[12]),
    .Cout(n1_bit_alu_13_cout), .Sub(in_3[3]), .Cin(n1_bit_alu_12_cout), .LessU(1'b0));  // open: SET
  _1_Bit_ALU u_1_bit_alu_14 (
    .OP(in_3[2:0]), .IN1(IN1[13]), .Less(1'b0), .IN2(IN2[13]), .OUT(n1_bit_alu_1_out[13]),
    .Cout(n1_bit_alu_14_cout), .Sub(in_3[3]), .Cin(n1_bit_alu_13_cout), .LessU(1'b0));  // open: SET
  _1_Bit_ALU u_1_bit_alu_15 (
    .OP(in_3[2:0]), .IN1(IN1[14]), .Less(1'b0), .IN2(IN2[14]), .OUT(n1_bit_alu_1_out[14]),
    .Cout(n1_bit_alu_15_cout), .Sub(in_3[3]), .Cin(n1_bit_alu_14_cout), .LessU(1'b0));  // open: SET
  _1_Bit_ALU u_1_bit_alu_16 (
    .OP(in_3[2:0]), .IN1(IN1[15]), .Less(1'b0), .IN2(IN2[15]), .OUT(n1_bit_alu_1_out[15]),
    .SET(n1_bit_alu_16_set), .Cout(n1_bit_alu_16_cout), .Sub(in_3[3]), .Cin(n1_bit_alu_15_cout), .LessU(1'b0));
  Shifter #(.width(16)) shifter_1 (.in(IN1), .\dist (IN2[3:0]), .out(shifter_1_out));
  Shifter #(.width(16), .shift("lr")) shifter_2 (.in(IN1), .\dist (IN2[3:0]), .out(shifter_2_out));
  Shifter #(.width(16), .shift("ar")) shifter_3 (.in(IN1), .\dist (IN2[3:0]), .out(shifter_3_out));
  Shifter #(.width(16), .shift("rl")) shifter_4 (.in(IN1), .\dist (IN2[3:0]), .out(shifter_4_out));
  not not_2 (not_2_out, n1_bit_alu_16_cout);
  or or_1 (or_1_out, n1_bit_alu_1_out[0], n1_bit_alu_1_out[1], n1_bit_alu_1_out[2], n1_bit_alu_1_out[3], n1_bit_alu_1_out[4], n1_bit_alu_1_out[5], n1_bit_alu_1_out[6], n1_bit_alu_1_out[7], n1_bit_alu_1_out[8], n1_bit_alu_1_out[9], n1_bit_alu_1_out[10], n1_bit_alu_1_out[11], n1_bit_alu_1_out[12], n1_bit_alu_1_out[13], n1_bit_alu_1_out[14]);
  or or_2 (or_2_out, Zero_flag, n1_bit_alu_16_set);
  or or_3 (or_3_out, Zero_flag, not_2_out);
  and and_1 (and_1_out, or_1_out, ~n1_bit_alu_1_out[15]);  // AND_Gate
  assign bit_extender_1_out = {{15{1'b0}}, or_2_out};  // Bit_Extender bit_extender_1
  assign bit_extender_2_out = {{15{1'b0}}, or_3_out};  // Bit_Extender bit_extender_2
  assign bit_extender_3_out = {{15{1'b0}}, and_1_out};  // Bit_Extender bit_extender_3
  nor nor_1 (Zero_flag, n1_bit_alu_1_out[0], n1_bit_alu_1_out[1], n1_bit_alu_1_out[2], n1_bit_alu_1_out[3], n1_bit_alu_1_out[4], n1_bit_alu_1_out[5], n1_bit_alu_1_out[6], n1_bit_alu_1_out[7], n1_bit_alu_1_out[8], n1_bit_alu_1_out[9], n1_bit_alu_1_out[10], n1_bit_alu_1_out[11], n1_bit_alu_1_out[12], n1_bit_alu_1_out[13], n1_bit_alu_1_out[14], n1_bit_alu_1_out[15]);
  Multiplexer #(.select(3), .width(16)) multiplexer_1 (
    .in0(n1_bit_alu_1_out), .in1(bit_extender_1_out), .in2(bit_extender_2_out), .in3(bit_extender_3_out),
    .in4(shifter_1_out), .in5(shifter_2_out), .in6(shifter_3_out), .in7(shifter_4_out), .out(OUT),
    .sel(in_3[6:4]));  // open: en

  // Other names for the same wires on the sheet: OP1[2:0] = in_3[2:0]; Sub = in_3[3]; OP2[2:0] = in_3[6:4]
endmodule

module Extender (
  input  [5:0] IN,
  input  Extender,
  output [15:0] OUT
);

  wire [15:0] bit_extender_1_out, bit_extender_2_out;

  assign bit_extender_1_out = {{10{1'b0}}, IN};  // Bit_Extender bit_extender_1
  assign bit_extender_2_out = {{10{IN[5]}}, IN};  // Bit_Extender bit_extender_2
  Multiplexer #(.width(16)) multiplexer_1 (
    .in0(bit_extender_1_out), .in1(bit_extender_2_out), .out(OUT), .sel(Extender));  // open: en
endmodule

module PC_Controller (
  input  Zero,
  input  [15:0] ALUOUT,
  input  JR,
  input  Jump,
  input  BNE,
  input  BEQ,
  input  BGT,
  input  BLT,
  input  BGTZ,
  input  BLTZ,
  input  BGEZ,
  input  BLEZ,
  output [1:0] PC_Controller,
  output Kill1,
  output Kill2
);

  wire and_1_out, and_2_out, and_3_out, and_4_out, and_5_out, and_6_out, and_7_out, and_8_out, and_9_out,
       and_10_out, or_1_out, or_5_out, or_6_out, or_8_out, or_9_out;

  and and_1 (and_1_out, ~Zero, BNE);  // AND_Gate
  or or_1 (or_1_out, and_1_out, and_2_out);
  and and_2 (and_2_out, Zero, BEQ);
  or or_2 (PC_Controller[1], and_3_out, and_4_out);
  and and_3 (and_3_out, JR, ~Kill2);  // AND_Gate
  or or_3 (PC_Controller[0], and_3_out, Kill2);
  and and_4 (and_4_out, Jump, ~Kill2);  // AND_Gate
  or or_4 (Kill2, or_1_out, or_5_out, or_6_out, or_8_out);
  or or_5 (or_5_out, and_6_out, and_5_out);
  and and_5 (and_5_out, ALUOUT[0], BLT);
  and and_6 (and_6_out, ALUOUT[0], BGT);
  or or_6 (or_6_out, and_7_out, and_8_out);
  and and_7 (and_7_out, ALUOUT[0], BGTZ);
  or or_7 (Kill1, and_3_out, and_4_out, Kill2);
  and and_8 (and_8_out, ALUOUT[0], BLTZ);
  and and_9 (and_9_out, or_9_out, BGEZ);
  or or_8 (or_8_out, and_9_out, and_10_out);
  and and_10 (and_10_out, or_9_out, BLEZ);
  or or_9 (or_9_out, Zero, ALUOUT[0]);

  // Other names for the same wires on the sheet: ALUOUT1BIT = ALUOUT[0]; Z = Zero
endmodule

module ALU_Control (
  input  [4:0] ALUOp,
  input  [2:0] Func,
  input  [3:0] OP,
  input  R_Type,
  output JR,
  output [1:0] MemToReg,
  output [7:0] ALUCntrl
);

  wire AND_out, JR_out, or_1_out, OR_2_out, priority_encoder_1_p3, priority_encoder_1_p4,
       priority_encoder_1_p5, priority_encoder_1_p7, priority_encoder_1_p8, priority_encoder_1_p9,
       priority_encoder_2_p2, priority_encoder_2_p3, priority_encoder_2_p4, priority_encoder_2_p8, SLL_out,
       SRA_out, SRL_out, SUB_out;
  wire [4:0] multiplexer_1_out;

  Multiplexer #(.width(5)) multiplexer_1 (
    .in0(ALUOp), .in1({OP[1:0], Func}), .out(multiplexer_1_out), .sel(R_Type));  // open: en
  or or_1 (or_1_out, 1'b1, AND_out);
  and AND (AND_out, ~multiplexer_1_out[4], ~multiplexer_1_out[3], ~multiplexer_1_out[2], ~multiplexer_1_out[1], ~multiplexer_1_out[0]);  // AND_Gate
  and OR_2 (OR_2_out, ~multiplexer_1_out[4], ~multiplexer_1_out[3], ~multiplexer_1_out[1], multiplexer_1_out[0]);  // AND_Gate
  // Priority_Encoder #(.select(4)) priority_encoder_1: pin names not known; wires that end beside it: or_1_out, OR_2_out, priority_encoder_1_p3, priority_encoder_1_p4, priority_encoder_1_p5, ALUCntrl[3:0], priority_encoder_1_p7, priority_encoder_1_p8, priority_encoder_1_p9
  and NOR (priority_encoder_1_p4, ~multiplexer_1_out[4], ~multiplexer_1_out[3], ~multiplexer_1_out[2], multiplexer_1_out[1], ~multiplexer_1_out[0]);  // AND_Gate
  and XOR (priority_encoder_1_p3, ~multiplexer_1_out[4], ~multiplexer_1_out[3], ~multiplexer_1_out[2], multiplexer_1_out[1], multiplexer_1_out[0]);  // AND_Gate
  and SLL (SLL_out, ~multiplexer_1_out[4], ~multiplexer_1_out[3], multiplexer_1_out[2], ~multiplexer_1_out[1], ~multiplexer_1_out[0]);  // AND_Gate
  and SRL (SRL_out, ~multiplexer_1_out[3], multiplexer_1_out[2], ~multiplexer_1_out[1], multiplexer_1_out[0]);  // AND_Gate
  and SRA (SRA_out, ~multiplexer_1_out[4], ~multiplexer_1_out[3], multiplexer_1_out[2], multiplexer_1_out[1], ~multiplexer_1_out[0]);  // AND_Gate
  // Priority_Encoder #(.select(4)) priority_encoder_2: pin names not known; wires that end beside it: 1'b1, priority_encoder_2_p2, priority_encoder_2_p3, priority_encoder_2_p4, SLL_out, SRL_out, SRA_out, priority_encoder_2_p8, ALUCntrl[7:4]
  and ROL (priority_encoder_2_p8, ~multiplexer_1_out[4], ~multiplexer_1_out[3], multiplexer_1_out[2], multiplexer_1_out[1], multiplexer_1_out[0]);  // AND_Gate
  and ADD (priority_encoder_1_p5, ~multiplexer_1_out[4], multiplexer_1_out[3], ~multiplexer_1_out[2], ~multiplexer_1_out[1], ~multiplexer_1_out[0]);  // AND_Gate
  or or_3 (priority_encoder_1_p7, SUB_out, priority_encoder_2_p3, priority_encoder_2_p2, priority_encoder_2_p4);
  and SUB (SUB_out, ~multiplexer_1_out[4], multiplexer_1_out[3], ~multiplexer_1_out[2], ~multiplexer_1_out[1], multiplexer_1_out[0]);  // AND_Gate
  and SLT (priority_encoder_1_p8, ~multiplexer_1_out[4], multiplexer_1_out[3], ~multiplexer_1_out[2], multiplexer_1_out[1], ~multiplexer_1_out[0]);  // AND_Gate
  and SLTU (priority_encoder_1_p9, ~multiplexer_1_out[4], multiplexer_1_out[3], ~multiplexer_1_out[2], multiplexer_1_out[1], multiplexer_1_out[0]);  // AND_Gate
  and SLTE (priority_encoder_2_p2, ~multiplexer_1_out[4], multiplexer_1_out[3], multiplexer_1_out[2], ~multiplexer_1_out[1], ~multiplexer_1_out[0]);  // AND_Gate
  and SLTEU (priority_encoder_2_p3, ~multiplexer_1_out[4], multiplexer_1_out[3], multiplexer_1_out[2], ~multiplexer_1_out[1], multiplexer_1_out[0]);  // AND_Gate
  and JALR (MemToReg[1], ~multiplexer_1_out[4], multiplexer_1_out[3], multiplexer_1_out[2], multiplexer_1_out[1], multiplexer_1_out[0]);  // AND_Gate
  and u_JR (JR_out, ~multiplexer_1_out[4], multiplexer_1_out[3], multiplexer_1_out[2], multiplexer_1_out[1], ~multiplexer_1_out[0]);  // AND_Gate
  or or_4 (JR, JR_out, MemToReg[1]);
  and BGT (priority_encoder_2_p4, multiplexer_1_out[4], ~multiplexer_1_out[3], ~multiplexer_1_out[2], ~multiplexer_1_out[1], ~multiplexer_1_out[0]);  // AND_Gate

  assign MemToReg[0] = 1'b0;

  // Other names for the same wires on the sheet: _1[3:0] = ALUCntrl[3:0]; _2[3:0] = ALUCntrl[7:4]
endmodule

module Control_Unit (
  input  [15:0] RD2,
  input  [3:0] OP,
  output LUI,
  output Jump,
  output BEQ,
  output BNE,
  output BLT,
  output BGT,
  output BLTZ,
  output BLEZ,
  output BGTZ,
  output BGEZ,
  output RegWrite,
  output [1:0] RegDest,
  output ALUSrc,
  output ExtOp,
  output MemWrite,
  output MemRead,
  output [1:0] MemToReg,
  output R_Type,
  output [4:0] ALUOp
);

  wire Add_out, ADDI_out, ANDI_out, BGEZ_out, BGTZ_out, BLEZ_out, BLTZ_out, GT_out, J_out, LT_out, or_2_out,
       or_8_out, ORI_out, R_Type_2_out, R_Type_out, Sub_out;
  wire [1:1] JAL_out;

  and u_R_Type (R_Type_out, ~OP[3], ~OP[2], ~OP[1], ~OP[0]);  // AND_Gate
  or or_1 (R_Type, R_Type_out, R_Type_2_out);
  and R_Type_2 (R_Type_2_out, ~OP[3], ~OP[2], ~OP[1], OP[0]);  // AND_Gate
  and SW (MemWrite, ~OP[3], ~OP[2], OP[1], OP[0]);  // AND_Gate
  and LW (MemRead, ~OP[3], ~OP[2], OP[1], ~OP[0]);  // AND_Gate
  and ANDI (ANDI_out, ~OP[3], OP[2], OP[1], ~OP[0]);  // AND_Gate
  and ORI (ORI_out, ~OP[3], OP[2], OP[1], OP[0]);  // AND_Gate
  and ADDI (ADDI_out, OP[3], ~OP[2], ~OP[1], ~OP[0]);  // AND_Gate
  and u_BNE (BNE, ~OP[3], OP[2], ~OP[1], OP[0]);  // AND_Gate
  and u_BEQ (BEQ, ~OP[3], OP[2], ~OP[1], ~OP[0]);  // AND_Gate
  and u_BLT (BLT, OP[3], OP[2], ~OP[1], OP[0]);  // AND_Gate
  and u_BGT (BGT, OP[3], OP[2], OP[1], OP[0]);
  and u_BLTZ (BLTZ_out, OP[3], OP[2], ~OP[1], ~OP[0]);  // AND_Gate
  and and_1 (BLTZ, BLTZ_out, ~RD2[0]);  // AND_Gate
  and u_BLEZ (BLEZ_out, OP[3], OP[2], ~OP[1], ~OP[0]);  // AND_Gate
  and and_2 (BLEZ, BLEZ_out, RD2[0]);
  and u_BGEZ (BGEZ_out, OP[3], OP[2], OP[1], ~OP[0]);  // AND_Gate
  and u_BGTZ (BGTZ_out, OP[3], OP[2], OP[1], ~OP[0]);  // AND_Gate
  and and_3 (BGTZ, BGTZ_out, ~RD2[0]);  // AND_Gate
  and and_4 (BGEZ, BGEZ_out, RD2[0]);
  and J (J_out, OP[3], ~OP[2], ~OP[1], OP[0]);  // AND_Gate
  and JAL (JAL_out[1], OP[3], ~OP[2], OP[1], OP[0]);  // AND_Gate
  and u_LUI (LUI, OP[3], ~OP[2], OP[1], ~OP[0]);  // AND_Gate
  or or_2 (or_2_out, R_Type_out, R_Type_2_out);
  or or_3 (Jump, JAL_out[1], J_out);
  or or_4 (RegWrite, LUI, R_Type_out, R_Type_2_out, MemRead, ANDI_out, ORI_out, ADDI_out, JAL_out[1]);
  or or_5 (RegDest[0], LUI, or_2_out);
  or or_6 (RegDest[1], LUI, JAL_out[1]);
  nor nor_1 (ALUSrc, BGEZ, R_Type_out, R_Type_2_out, BEQ, BNE, BLEZ, BLT, BGT, BLTZ, BGTZ);
  nor nor_2 (ExtOp, ORI_out, ANDI_out);
  or Add (Add_out, MemRead, MemWrite, ADDI_out);
  or Sub (Sub_out, BEQ, BNE);
  assign MemToReg = {1'b0, MemRead} | {2{LUI}} | {JAL_out[1], 1'b0};  // OR_Gate or_7, 2 bits wide
  or LT (LT_out, BLT, BLEZ, BLTZ);
  or GT (GT_out, BGT, BGEZ, BGTZ);
  or or_8 (or_8_out, 1'b1, ANDI_out);
  // Priority_Encoder #(.select(5)) priority_encoder_1: pin names not known; wires that end beside it: or_8_out, ORI_out, Add_out, Sub_out, LT_out, ALUOp, GT_out

  // Notes on the sheet:
  //   OR
  //   AND
endmodule

module IF_ID (
  input  [11:0] in_1,
  input  [15:0] in_2,
  input  CLk,
  input  En,
  input  Clr,
  output [11:0] out_6,
  output [15:0] out_7
);

  Register #(.width(12)) register_1 (.D(in_1), .en(En), .Q(out_6), .clk(CLk), .clr(Clr));
  Register #(.width(16)) register_2 (.D(in_2), .en(En), .Q(out_7), .clk(CLk), .clr(Clr));
endmodule

module ID_EX (
  input  [11:0] in_1,
  input  [11:0] in_2,
  input  [11:0] in_3,
  input  [15:0] in_4,
  input  [15:0] in_5,
  input  [15:0] in_6,
  input  [2:0] in_7,
  input  CLK,
  input  Clr,
  input  En,
  input  in_11,
  input  [1:0] in_12,
  input  in_13,
  input  in_14,
  input  in_15,
  input  in_16,
  input  in_17,
  input  in_18,
  input  in_19,
  input  in_20,
  input  in_21,
  input  in_22,
  input  in_23,
  input  [7:0] in_24,
  input  in_25,
  output [11:0] out_26,
  output [11:0] out_27,
  output [11:0] out_28,
  output [15:0] out_29,
  output [15:0] out_30,
  output [15:0] out_31,
  output [2:0] out_32,
  output out_33,
  output [1:0] out_34,
  output out_35,
  output out_36,
  output out_37,
  output out_38,
  output out_39,
  output out_40,
  output out_41,
  output out_42,
  output out_43,
  output out_44,
  output out_45,
  output [7:0] out_46,
  output out_47
);

  Register #(.width(12)) register_1 (.D(in_1), .en(En), .Q(out_26), .clk(CLK), .clr(Clr));
  Register #(.width(12)) register_2 (.D(in_2), .en(En), .Q(out_27), .clk(CLK), .clr(Clr));
  Register #(.width(12)) register_3 (.D(in_3), .en(En), .Q(out_28), .clk(CLK), .clr(Clr));
  Register #(.width(16)) register_4 (.D(in_4), .en(En), .Q(out_29), .clk(CLK), .clr(Clr));
  Register #(.width(16)) register_5 (.D(in_5), .en(En), .Q(out_30), .clk(CLK), .clr(Clr));
  Register #(.width(16)) register_6 (.D(in_6), .en(En), .Q(out_31), .clk(CLK), .clr(Clr));
  Register #(.width(3)) register_7 (.D(in_7), .en(En), .Q(out_32), .clk(CLK), .clr(Clr));
  Register #(.width(1)) register_8 (.D(in_11), .en(En), .Q(out_33), .clk(CLK), .clr(Clr));
  Register #(.width(2)) register_9 (.D(in_12), .en(En), .Q(out_34), .clk(CLK), .clr(Clr));
  Register #(.width(1)) register_10 (.D(in_13), .en(En), .Q(out_35), .clk(CLK), .clr(Clr));
  Register #(.width(1)) register_11 (.D(in_14), .en(En), .Q(out_36), .clk(CLK), .clr(Clr));
  Register #(.width(1)) register_12 (.D(in_15), .en(En), .Q(out_37), .clk(CLK), .clr(Clr));
  Register #(.width(1)) register_13 (.D(in_16), .en(En), .Q(out_38), .clk(CLK), .clr(Clr));
  Register #(.width(1)) register_14 (.D(in_17), .en(En), .Q(out_39), .clk(CLK), .clr(Clr));
  Register #(.width(1)) register_15 (.D(in_18), .en(En), .Q(out_40), .clk(CLK), .clr(Clr));
  Register #(.width(1)) register_16 (.D(in_19), .en(En), .Q(out_41), .clk(CLK), .clr(Clr));
  Register #(.width(1)) register_17 (.D(in_20), .en(En), .Q(out_42), .clk(CLK), .clr(Clr));
  Register #(.width(1)) register_18 (.D(in_21), .en(En), .Q(out_43), .clk(CLK), .clr(Clr));
  Register #(.width(1)) register_19 (.D(in_22), .en(En), .Q(out_44), .clk(CLK), .clr(Clr));
  Register #(.width(1)) register_20 (.D(in_23), .en(En), .Q(out_45), .clk(CLK), .clr(Clr));
  Register register_21 (.D(in_24), .en(En), .Q(out_46), .clk(CLK), .clr(Clr));
  Register #(.width(1)) register_22 (.D(in_25), .en(En), .Q(out_47), .clk(CLK), .clr(Clr));
endmodule

module EX_MEM (
  input  [11:0] in_1,
  input  [15:0] in_2,
  input  [15:0] in_3,
  input  [15:0] in_4,
  input  [2:0] in_5,
  input  Clr,
  input  CLK,
  input  EN,
  input  in_9,
  input  [1:0] in_10,
  input  in_11,
  input  in_12,
  output [11:0] out_13,
  output [15:0] out_14,
  output [15:0] out_15,
  output [15:0] out_16,
  output [2:0] out_17,
  output out_18,
  output [1:0] out_19,
  output out_20,
  output out_21
);

  Register #(.width(12)) register_1 (.D(in_1), .en(EN), .Q(out_13), .clk(CLK), .clr(Clr));
  Register #(.width(16)) register_2 (.D(in_2), .en(EN), .Q(out_14), .clk(CLK), .clr(Clr));
  Register #(.width(16)) register_3 (.D(in_3), .en(EN), .Q(out_15), .clk(CLK), .clr(Clr));
  Register #(.width(16)) register_4 (.D(in_4), .en(EN), .Q(out_16), .clk(CLK), .clr(Clr));
  Register #(.width(3)) register_5 (.D(in_5), .en(EN), .Q(out_17), .clk(CLK), .clr(Clr));
  Register #(.width(1)) register_6 (.D(in_9), .en(EN), .Q(out_18), .clk(CLK), .clr(Clr));
  Register #(.width(2)) register_7 (.D(in_10), .en(EN), .Q(out_19), .clk(CLK), .clr(Clr));
  Register #(.width(1)) register_8 (.D(in_11), .en(EN), .Q(out_20), .clk(CLK), .clr(Clr));
  Register #(.width(1)) register_9 (.D(in_12), .en(EN), .Q(out_21), .clk(CLK), .clr(Clr));
endmodule

module MEM_WB (
  input  [15:0] in_1,
  input  [2:0] in_2,
  input  CLK,
  input  En,
  input  Clr,
  input  in_6,
  output [15:0] out_7,
  output [2:0] out_8,
  output out_9
);

  Register #(.width(16)) register_1 (.D(in_1), .en(En), .Q(out_7), .clk(CLK), .clr(Clr));
  Register #(.width(3)) register_2 (.D(in_2), .en(En), .Q(out_8), .clk(CLK), .clr(Clr));
  Register #(.width(1)) register_3 (.D(in_6), .en(En), .Q(out_9), .clk(CLK), .clr(Clr));
endmodule

module Main_Control_Unit (
  input  [15:0] RD2,
  input  [3:0] OP,
  input  [2:0] FUNC,
  output [7:0] ALUOP,
  output LUI,
  output J,
  output BEQ,
  output BNE,
  output BLT,
  output BGT,
  output BLTZ,
  output BLEZ,
  output [1:0] MemToReg,
  output JR,
  output RegWrite,
  output [1:0] RegDest,
  output ALUSrc,
  output ExtOP,
  output MemW,
  output MemR,
  output BGTZ,
  output BGEZ
);

  wire control_unit_1_r_type;
  wire [1:0] alu_control_1_memtoreg, control_unit_1_memtoreg;
  wire [4:0] control_unit_1_aluop;

  Control_Unit control_unit_1 (
    .OP(OP), .Jump(J), .BEQ(BEQ), .BNE(BNE), .BLT(BLT), .BGT(BGT), .BLTZ(BLTZ), .BLEZ(BLEZ), .BGTZ(BGTZ),
    .BGEZ(BGEZ), .RegWrite(RegWrite), .RegDest(RegDest), .ALUSrc(ALUSrc), .ExtOp(ExtOP), .MemWrite(MemW),
    .MemRead(MemR), .MemToReg(control_unit_1_memtoreg), .R_Type(control_unit_1_r_type),
    .ALUOp(control_unit_1_aluop), .RD2(RD2), .LUI(LUI));
  assign MemToReg = control_unit_1_memtoreg | alu_control_1_memtoreg;  // OR_Gate or_1, 2 bits wide
  ALU_Control alu_control_1 (
    .ALUOp(control_unit_1_aluop), .Func(FUNC), .OP(OP), .JR(JR), .MemToReg(alu_control_1_memtoreg),
    .R_Type(control_unit_1_r_type), .ALUCntrl(ALUOP));
endmodule

module Hazard_Detect_Forward_and_Stall (
  input  [2:0] RS,
  input  [2:0] Rt,
  input  RegWrite_EX,
  input  [2:0] Rd_EX,
  input  RegWrite_MEM,
  input  [2:0] Rd_MEM,
  input  RegWrite_Wb,
  input  [2:0] Rd_Wb,
  input  EX_MemRd,
  output [1:0] Forward_A,
  output [1:0] Forward_B,
  output Stall
);

  wire and_1_out, and_2_out, and_4_out, and_5_out, and_6_out, and_7_out, and_8_out, and_9_out, and_10_out,
       and_11_out, and_12_out, and_13_out, comparator_1_eq, comparator_2_eq, comparator_3_eq,
       comparator_4_eq, comparator_5_eq, comparator_6_eq, comparator_7_eq, comparator_8_eq, comparator_9_eq,
       or_1_out, or_2_out, or_3_out;

  and and_1 (and_1_out, Forward_B[0], ~Forward_B[1]);  // AND_Gate
  and and_2 (and_2_out, Forward_A[0], ~Forward_A[1]);  // AND_Gate
  Comparator #(.width(3)) comparator_1 (.a(3'b000), .b(Rd_EX), .eq(comparator_1_eq));  // open: gt, lt
  Comparator #(.width(3)) comparator_2 (.a(Rd_EX), .b(RS), .eq(comparator_2_eq));  // open: gt, lt
  Comparator #(.width(3)) comparator_3 (.a(Rd_EX), .b(Rt), .eq(comparator_3_eq));  // open: gt, lt
  Comparator #(.width(3)) comparator_4 (.a(3'b000), .b(Rd_MEM), .eq(comparator_4_eq));  // open: gt, lt
  Comparator #(.width(3)) comparator_5 (.a(Rd_MEM), .b(RS), .eq(comparator_5_eq));  // open: gt, lt
  Comparator #(.width(3)) comparator_6 (.a(Rd_MEM), .b(Rt), .eq(comparator_6_eq));  // open: gt, lt
  Comparator #(.width(3)) comparator_7 (.a(3'b000), .b(Rd_Wb), .eq(comparator_7_eq));  // open: gt, lt
  Comparator #(.width(3)) comparator_8 (.a(Rd_Wb), .b(RS), .eq(comparator_8_eq));  // open: gt, lt
  Comparator #(.width(3)) comparator_9 (.a(Rd_Wb), .b(Rt), .eq(comparator_9_eq));  // open: gt, lt
  or or_1 (or_1_out, and_1_out, and_2_out);
  and and_3 (Stall, EX_MemRd, or_1_out);
  and and_4 (and_4_out, RegWrite_EX, ~comparator_1_eq, comparator_2_eq);  // AND_Gate
  and and_5 (and_5_out, RegWrite_EX, ~comparator_1_eq, comparator_3_eq);  // AND_Gate
  and and_6 (and_6_out, RegWrite_MEM, ~comparator_4_eq, comparator_5_eq);  // AND_Gate
  and and_7 (and_7_out, RegWrite_MEM, ~comparator_4_eq, comparator_6_eq);  // AND_Gate
  and and_8 (and_8_out, RegWrite_Wb, ~comparator_7_eq, comparator_8_eq);  // AND_Gate
  and and_9 (and_9_out, RegWrite_Wb, ~comparator_7_eq, comparator_9_eq);  // AND_Gate
  or or_2 (or_2_out, and_8_out, and_6_out);
  or or_3 (or_3_out, and_9_out, and_7_out);
  and and_10 (and_10_out, and_4_out, or_2_out);
  and and_11 (and_11_out, and_5_out, or_3_out);
  and and_12 (and_12_out, ~and_10_out, and_6_out);  // AND_Gate
  and and_13 (and_13_out, ~and_11_out, and_7_out);  // AND_Gate
  or or_4 (Forward_A[0], and_4_out, and_10_out, and_8_out);
  or or_5 (Forward_A[1], and_12_out, and_8_out);
  or or_6 (Forward_B[0], and_5_out, and_11_out, and_9_out);
  or or_7 (Forward_B[1], and_13_out, and_9_out);
endmodule
