// Logisim project Single Cycle V1 (1).circ as structural Verilog: 8 circuits, main circuit main
module main (
  input  [3:0] in_1,
  input  [2:0] in_2,
  output [15:0] out_3,
  output [2:0] out_4,
  output [1:0] out_5,
  output [1:0] out_6
);

  wire ALUSrc, BEQ, BGEZ, BGT, BGTZ, BLEZ, BLT, BLTZ, BNE, CLK, ExtOp, J, JR, main_control_unit_1_r_type,
       MemRead, MemWrite, pull_resistor_1_node, RegWrite, Zero;
  wire [1:0] alu_control_1_memtoreg, main_control_unit_1_memtoreg;
  wire [2:0] Funct, multiplexer_2_out;
  wire [3:0] Opcode;
  wire [4:0] main_control_unit_1_aluop;
  wire [7:0] ALUCntrl;
  wire [11:0] adder_1_out, adder_2_out, extender_1_out, multiplexer_1_out, register_1_q;
  wire [11:3] ram_1_data;
  wire [15:0] ALUOUT, multiplexer_3_out, ram_2_data, RD2, register1_1_rd1, shifter_1_out;
  wire [15:12] extender_1_out_2;

  Multiplexer #(.select(3), .width(12)) multiplexer_1 (
    .in0(adder_1_out), .in1(adder_2_out), .in2({ram_1_data, Funct}), .in4(register1_1_rd1[11:0]),
    .out(multiplexer_1_out), .sel(out_4));  // open: in3, in5, in6, in7, en
  PC_Controller pc_controller_1 (
    .PC_Controller(out_4), .Zero_2(Zero), .Jump(J), .BNE(BNE), .BEQ(BEQ), .BGT(BGT), .BLT(BLT),
    .ALUOUT_2(ALUOUT), .JR(JR), .BGEZ(BGEZ), .BLEZ(BLEZ), .ALUOUT(ALUOUT), .BGTZ(BGTZ), .BLTZ(BLTZ),
    .ALUOUT_3(ALUOUT), .Zero(Zero));
  Register #(.width(12)) register_1 (.D(multiplexer_1_out), .Q(register_1_q), .clk(CLK));  // open: en, clr
  Adder #(.width(12)) adder_1 (.a(register_1_q), .b(12'h1), .out(adder_1_out));  // open: cin, cout
  Pull_Resistor #(.pull(1)) pull_resistor_1 (.node(pull_resistor_1_node));
  Clock clock_1 (.out(CLK));
  RAM #(.addrWidth(12), .dataWidth(16)) ram_1 (
    .addr(register_1_q), .data({Opcode, ram_1_data, Funct}), .ld(pull_resistor_1_node));  // open: sel, clk, clr
  Main_Control_Unit main_control_unit_1 (
    .OP(Opcode), .Jump(J), .BEQ(BEQ), .BNE(BNE), .BLT(BLT), .BGT(BGT), .BLTZ(BLTZ), .BLEZ(BLEZ), .BGTZ(BGTZ),
    .BGEZ(BGEZ), .RegWrite(RegWrite), .RegDest(out_6), .ALUSrc(ALUSrc), .ExtOp(ExtOp), .MemWrite(MemWrite),
    .MemRead(MemRead), .MemToReg(main_control_unit_1_memtoreg), .R_Type(main_control_unit_1_r_type),
    .ALUOp(main_control_unit_1_aluop), .RD2(RD2));
  Multiplexer #(.select(2), .width(3)) multiplexer_2 (
    .in0(ram_1_data[8:6]), .in1(ram_1_data[5:3]), .in2(3'b111), .in3(3'b001), .out(multiplexer_2_out),
    .sel(out_6));  // open: en
  Register1 register1_1 (
    .R1(ram_1_data[11:9]), .R2(ram_1_data[8:6]), .W1(out_3), .RW(multiplexer_2_out), .CLK(CLK),
    .RD1(register1_1_rd1), .RD2(RD2), .WE(RegWrite));
  Extender extender_1 (.IN({ram_1_data[5:3], Funct}), .OUT({extender_1_out_2, extender_1_out}), .Extender(ExtOp));
  Shifter #(.width(16)) shifter_1 (.in({4'b0000, ram_1_data, Funct}), .\dist (4'b0100), .out(shifter_1_out));
  Multiplexer #(.width(16)) multiplexer_3 (
    .in0(RD2), .in1({extender_1_out_2, extender_1_out}), .out(multiplexer_3_out), .sel(ALUSrc));  // open: en
  Adder #(.width(12)) adder_2 (.a(adder_1_out), .b(extender_1_out), .out(adder_2_out));  // open: cin, cout
  _16_Bit_ALU u_16_bit_alu_1 (
    .IN1(register1_1_rd1), .IN2(multiplexer_3_out), .Zero_flag(Zero), .OUT(ALUOUT), .in_3(ALUCntrl));
  assign out_5 = main_control_unit_1_memtoreg | alu_control_1_memtoreg;  // OR_Gate or_1, 2 bits wide
  ALU_Control alu_control_1 (
    .ALUOp(main_control_unit_1_aluop), .Func(Funct), .OP(Opcode), .JR(JR), .MemToReg(alu_control_1_memtoreg),
    .R_Type(main_control_unit_1_r_type), .ALUCntrl(ALUCntrl));
  RAM #(.addrWidth(12), .dataWidth(16), .bus("separate")) ram_2 (
    .addr(ALUOUT[11:0]), .din(RD2), .data(ram_2_data), .str(MemWrite), .clk(CLK), .ld(MemRead));  // open: sel, clr
  Multiplexer #(.select(2), .width(16)) multiplexer_4 (
    .in0(ALUOUT), .in1(ram_2_data), .in2({4'b0000, adder_1_out}), .in3(shifter_1_out), .out(out_3),
    .sel(out_5));  // open: en

  // Other names for the same wires on the sheet: MemToReg[1:0] = out_5; RegDest[1:0] = out_6

  // Notes on the sheet:
  //   JR
  //   J
  //   Branch
  //   PC+1
  //   LUI
endmodule

module Register1 (
  input  [2:0] R1,
  input  [2:0] R2,
  input  [15:0] W1,
  input  [2:0] RW,
  input  WE,
  input  CLK,
  output [15:0] RD1,
  output [15:0] RD2
);

  wire demultiplexer_2_out0, demultiplexer_2_out1, demultiplexer_2_out2, demultiplexer_2_out3,
       demultiplexer_2_out4, demultiplexer_2_out5, demultiplexer_2_out6, demultiplexer_2_out7;
  wire [15:0] demultiplexer_1_out1, demultiplexer_1_out2, demultiplexer_1_out3, demultiplexer_1_out4,
       demultiplexer_1_out5, demultiplexer_1_out6, demultiplexer_1_out7, register_1_q, register_2_q,
       register_3_q, register_4_q, register_5_q, register_6_q, register_7_q, register_8_q;

  Demultiplexer #(.select(3), .width(16)) demultiplexer_1 (
    .out1(demultiplexer_1_out1), .out2(demultiplexer_1_out2), .out3(demultiplexer_1_out3),
    .out4(demultiplexer_1_out4), .out5(demultiplexer_1_out5), .out6(demultiplexer_1_out6),
    .out7(demultiplexer_1_out7), .in(W1), .sel(RW));  // open: out0, en
  Demultiplexer #(.select(3)) demultiplexer_2 (
    .out0(demultiplexer_2_out0), .out1(demultiplexer_2_out1), .out2(demultiplexer_2_out2),
    .out3(demultiplexer_2_out3), .out4(demultiplexer_2_out4), .out5(demultiplexer_2_out5),
    .out6(demultiplexer_2_out6), .out7(demultiplexer_2_out7), .in(WE), .sel(RW));  // open: en
  Register #(.width(16)) register_1 (
    .D({16{1'b0}}), .en(demultiplexer_2_out0), .Q(register_1_q), .clk(CLK));  // open: clr
  Register #(.width(16)) register_2 (
    .D(demultiplexer_1_out1), .en(demultiplexer_2_out1), .Q(register_2_q), .clk(CLK));  // open: clr
  Register #(.width(16)) register_3 (
    .D(demultiplexer_1_out2), .en(demultiplexer_2_out2), .Q(register_3_q), .clk(CLK));  // open: clr
  Register #(.width(16)) register_4 (
    .D(demultiplexer_1_out3), .en(demultiplexer_2_out3), .Q(register_4_q), .clk(CLK));  // open: clr
  Register #(.width(16)) register_5 (
    .D(demultiplexer_1_out4), .en(demultiplexer_2_out4), .Q(register_5_q), .clk(CLK));  // open: clr
  Register #(.width(16)) register_6 (
    .D(demultiplexer_1_out5), .en(demultiplexer_2_out5), .Q(register_6_q), .clk(CLK));  // open: clr
  Register #(.width(16)) register_7 (
    .D(demultiplexer_1_out6), .en(demultiplexer_2_out6), .Q(register_7_q), .clk(CLK));  // open: clr
  Register #(.width(16)) register_8 (
    .D(demultiplexer_1_out7), .en(demultiplexer_2_out7), .Q(register_8_q), .clk(CLK));  // open: clr
  Multiplexer #(.select(3), .width(16)) multiplexer_1 (
    .in0(register_1_q), .in1(register_2_q), .in2(register_3_q), .in3(register_4_q), .in4(register_5_q),
    .in5(register_6_q), .in6(register_7_q), .in7(register_8_q), .out(RD1), .sel(R1));  // open: en
  Multiplexer #(.select(3), .width(16)) multiplexer_2 (
    .in0(register_1_q), .in1(register_2_q), .in2(register_3_q), .in3(register_4_q), .in4(register_5_q),
    .in5(register_6_q), .in6(register_7_q), .in7(register_8_q), .out(RD2), .sel(R2));  // open: en
endmodule

module _1_Bit_ALU (
  input  [2:0] OP,
  input  Sub,
  input  Cin,
  input  IN1,
  input  Less,
  input  LessU,
  input  IN2,
  output OUT,
  output SET,
  output Cout
);

  wire and_1_out, nor_1_out, or_1_out, xor_1_out, xor_2_out;

  xor xor_1 (xor_1_out, IN2, Sub);
  and and_1 (and_1_out, IN1, IN2);
  or or_1 (or_1_out, IN1, IN2);
  xor xor_2 (xor_2_out, IN1, IN2);
  nor nor_1 (nor_1_out, IN1, IN2);
  Adder #(.width(1)) adder_1 (.a(IN1), .b(xor_1_out), .out(SET), .cin(Cin), .cout(Cout));
  Multiplexer #(.select(3)) multiplexer_1 (
    .in0(and_1_out), .in1(or_1_out), .in2(xor_2_out), .in3(nor_1_out), .in4(SET), .in5(Less), .in6(LessU),
    .out(OUT), .sel(OP));  // open: in7, en
endmodule

module _16_Bit_ALU (
  input  [15:0] IN1,
  input  [15:0] IN2,
  input  [7:0] in_3,
  output Zero_flag,
  output [15:0] OUT
);

  wire and_1_out, n1_bit_alu_1_cout, n1_bit_alu_2_cout, n1_bit_alu_3_cout, n1_bit_alu_4_cout,
       n1_bit_alu_5_cout, n1_bit_alu_6_cout, n1_bit_alu_7_cout, n1_bit_alu_8_cout, n1_bit_alu_9_cout,
       n1_bit_alu_10_cout, n1_bit_alu_11_cout, n1_bit_alu_12_cout, n1_bit_alu_13_cout, n1_bit_alu_14_cout,
       n1_bit_alu_15_cout, n1_bit_alu_16_cout, n1_bit_alu_16_set, not_1_out, not_2_out, or_1_out, or_2_out,
       or_3_out;
  wire [15:0] bit_extender_1_out, bit_extender_2_out, bit_extender_3_out, n1_bit_alu_1_out, shifter_1_out,
       shifter_2_out, shifter_3_out, shifter_4_out;

  not not_1 (not_1_out, n1_bit_alu_16_cout);
  _1_Bit_ALU u_1_bit_alu_1 (
    .OP(in_3[2:0]), .IN1(IN1[0]), .Less(n1_bit_alu_16_set), .IN2(IN2[0]), .OUT(n1_bit_alu_1_out[0]),
    .Cout(n1_bit_alu_1_cout), .Sub(in_3[3]), .Cin(in_3[3]), .LessU(not_1_out));  // open: SET
  _1_Bit_ALU u_1_bit_alu_2 (
    .OP(in_3[2:0]), .IN1(IN1[1]), .Less(1'b0), .IN2(IN2[1]), .OUT(n1_bit_alu_1_out[1]),
    .Cout(n1_bit_alu_2_cout), .Sub(in_3[3]), .Cin(n1_bit_alu_1_cout), .LessU(1'b0));  // open: SET
  _1_Bit_ALU u_1_bit_alu_3 (
    .OP(in_3[2:0]), .IN1(IN1[2]), .Less(1'b0), .IN2(IN2[2]), .OUT(n1_bit_alu_1_out[2]),
    .Cout(n1_bit_alu_3_cout), .Sub(in_3[3]), .Cin(n1_bit_alu_2_cout), .LessU(1'b0));  // open: SET
  _1_Bit_ALU u_1_bit_alu_4 (
    .OP(in_3[2:0]), .IN1(IN1[3]), .Less(1'b0), .IN2(IN2[3]), .OUT(n1_bit_alu_1_out[3]),
    .Cout(n1_bit_alu_4_cout), .Sub(in_3[3]), .Cin(n1_bit_alu_3_cout), .LessU(1'b0));  // open: SET
  _1_Bit_ALU u_1_bit_alu_5 (
    .OP(in_3[2:0]), .IN1(IN1[4]), .Less(1'b0), .IN2(IN2[4]), .OUT(n1_bit_alu_1_out[4]),
    .Cout(n1_bit_alu_5_cout), .Sub(in_3[3]), .Cin(n1_bit_alu_4_cout), .LessU(1'b0));  // open: SET
  _1_Bit_ALU u_1_bit_alu_6 (
    .OP(in_3[2:0]), .IN1(IN1[5]), .Less(1'b0), .IN2(IN2[5]), .OUT(n1_bit_alu_1_out[5]),
    .Cout(n1_bit_alu_6_cout), .Sub(in_3[3]), .Cin(n1_bit_alu_5_cout), .LessU(1'b0));  // open: SET
  _1_Bit_ALU u_1_bit_alu_7 (
    .OP(in_3[2:0]), .IN1(IN1[6]), .Less(1'b0), .IN2(IN2[6]), .OUT(n1_bit_alu_1_out[6]),
    .Cout(n1_bit_alu_7_cout), .Sub(in_3[3]), .Cin(n1_bit_alu_6_cout), .LessU(1'b0));  // open: SET
  _1_Bit_ALU u_1_bit_alu_8 (
    .OP(in_3[2:0]), .IN1(IN1[7]), .Less(1'b0), .IN2(IN2[7]), .OUT(n1_bit_alu_1_out[7]),
    .Cout(n1_bit_alu_8_cout), .Sub(in_3[3]), .Cin(n1_bit_alu_7_cout), .LessU(1'b0));  // open: SET
  _1_Bit_ALU u_1_bit_alu_9 (
    .OP(in_3[2:0]), .IN1(IN1[8]), .Less(1'b0), .IN2(IN2[8]), .OUT(n1_bit_alu_1_out[8]),
    .Cout(n1_bit_alu_9_cout), .Sub(in_3[3]), .Cin(n1_bit_alu_8_cout), .LessU(1'b0));  // open: SET
  _1_Bit_ALU u_1_bit_alu_10 (
    .OP(in_3[2:0]), .IN1(IN1[9]), .Less(1'b0), .IN2(IN2[9]), .OUT(n1_bit_alu_1_out[9]),
    .Cout(n1_bit_alu_10_cout), .Sub(in_3[3]), .Cin(n1_bit_alu_9_cout), .LessU(1'b0));  // open: SET
  _1_Bit_ALU u_1_bit_alu_11 (
    .OP(in_3[2:0]), .IN1(IN1[10]), .Less(1'b0), .IN2(IN2[10]), .OUT(n1_bit_alu_1_out[10]),
    .Cout(n1_bit_alu_11_cout), .Sub(in_3[3]), .Cin(n1_bit_alu_10_cout), .LessU(1'b0));  // open: SET
  _1_Bit_ALU u_1_bit_alu_12 (
    .OP(in_3[2:0]), .IN1(IN1[11]), .Less(1'b0), .IN2(IN2[11]), .OUT(n1_bit_alu_1_out[11]),
    .Cout(n1_bit_alu_12_cout), .Sub(in_3[3]), .Cin(n1_bit_alu_11_cout), .LessU(1'b0));  // open: SET
  _1_Bit_ALU u_1_bit_alu_13 (
    .OP(in_3[2:0]), .IN1(IN1[12]), .Less(1'b0), .IN2(IN2[12]), .OUT(n1_bit_alu_1_out[12]),
    .Cout(n1_bit_alu_13_cout), .Sub(in_3[3]), .Cin(n1_bit_alu_12_cout), .LessU(1'b0));  // open: SET
  _1_Bit_ALU u_1_bit_alu_14 (
    .OP(in_3[2:0]), .IN1(IN1[13]), .Less(1'b0), .IN2(IN2[13]), .OUT(n1_bit_alu_1_out[13]),
    .Cout(n1_bit_alu_14_cout), .Sub(in_3[3]), .Cin(n1_bit_alu_13_cout), .LessU(1'b0));  // open: SET
  _1_Bit_ALU u_1_bit_alu_15 (
    .OP(in_3[2:0]), .IN1(IN1[14]), .Less(1'b0), .IN2(IN2[14]), .OUT(n1_bit_alu_1_out[14]),
    .Cout(n1_bit_alu_15_cout), .Sub(in_3[3]), .Cin(n1_bit_alu_14_cout), .LessU(1'b0));  // open: SET
  _1_Bit_ALU u_1_bit_alu_16 (
    .OP(in_3[2:0]), .IN1(IN1[15]), .Less(1'b0), .IN2(IN2[15]), .OUT(n1_bit_alu_1_out[15]),
    .SET(n1_bit_alu_16_set), .Cout(n1_bit_alu_16_cout), .Sub(in_3[3]), .Cin(n1_bit_alu_15_cout), .LessU(1'b0));
  Shifter #(.width(16)) shifter_1 (.in(IN1), .\dist (IN2[3:0]), .out(shifter_1_out));
  Shifter #(.width(16), .shift("lr")) shifter_2 (.in(IN1), .\dist (IN2[3:0]), .out(shifter_2_out));
  Shifter #(.width(16), .shift("ar")) shifter_3 (.in(IN1), .\dist (IN2[3:0]), .out(shifter_3_out));
  Shifter #(.width(16), .shift("rl")) shifter_4 (.in(IN1), .\dist (IN2[3:0]), .out(shifter_4_out));
  not not_2 (not_2_out, n1_bit_alu_16_cout);
  or or_1 (or_1_out, n1_bit_alu_1_out[0], n1_bit_alu_1_out[1], n1_bit_alu_1_out[2], n1_bit_alu_1_out[3], n1_bit_alu_1_out[4], n1_bit_alu_1_out[5], n1_bit_alu_1_out[6], n1_bit_alu_1_out[7], n1_bit_alu_1_out[8], n1_bit_alu_1_out[9], n1_bit_alu_1_out[10], n1_bit_alu_1_out[11], n1_bit_alu_1_out[12], n1_bit_alu_1_out[13], n1_bit_alu_1_out[14]);
  or or_2 (or_2_out, Zero_flag, n1_bit_alu_16_set);
  or or_3 (or_3_out, Zero_flag, not_2_out);
  and and_1 (and_1_out, or_1_out, ~n1_bit_alu_1_out[15]);  // AND_Gate
  assign bit_extender_1_out = {{15{1'b0}}, or_2_out};  // Bit_Extender bit_extender_1
  assign bit_extender_2_out = {{15{1'b0}}, or_3_out};  // Bit_Extender bit_extender_2
  assign bit_extender_3_out = {{15{1'b0}}, and_1_out};  // Bit_Extender bit_extender_3
  nor nor_1 (Zero_flag, n1_bit_alu_1_out[0], n1_bit_alu_1_out[1], n1_bit_alu_1_out[2], n1_bit_alu_1_out[3], n1_bit_alu_1_out[4], n1_bit_alu_1_out[5], n1_bit_alu_1_out[6], n1_bit_alu_1_out[7], n1_bit_alu_1_out[8], n1_bit_alu_1_out[9], n1_bit_alu_1_out[10], n1_bit_alu_1_out[11], n1_bit_alu_1_out[12], n1_bit_alu_1_out[13], n1_bit_alu_1_out[14], n1_bit_alu_1_out[15]);
  Multiplexer #(.select(3), .width(16)) multiplexer_1 (
    .in0(n1_bit_alu_1_out), .in1(bit_extender_1_out), .in2(bit_extender_2_out), .in3(bit_extender_3_out),
    .in4(shifter_1_out), .in5(shifter_2_out), .in6(shifter_3_out), .in7(shifter_4_out), .out(OUT),
    .sel(in_3[6:4]));  // open: en

  // Other names for the same wires on the sheet: OP1[2:0] = in_3[2:0]; Sub = in_3[3]; OP2[2:0] = in_3[6:4]
endmodule

module Extender (
  input  [5:0] IN,
  input  Extender,
  output [15:0] OUT
);

  wire [15:0] bit_extender_1_out, bit_extender_2_out;

  assign bit_extender_1_out = {{10{1'b0}}, IN};  // Bit_Extender bit_extender_1
  assign bit_extender_2_out = {{10{IN[5]}}, IN};  // Bit_Extender bit_extender_2
  Multiplexer #(.width(16)) multiplexer_1 (
    .in0(bit_extender_1_out), .in1(bit_extender_2_out), .out(OUT), .sel(Extender));  // open: en
endmodule

module PC_Controller (
  input  Zero,
  input  Zero_2,
  input  [15:0] ALUOUT,
  input  [15:0] ALUOUT_2,
  input  [15:0] ALUOUT_3,
  input  JR,
  input  Jump,
  input  BNE,
  input  BEQ,
  input  BGT,
  input  BLT,
  input  BGTZ,
  input  BLTZ,
  input  BGEZ,
  input  BLEZ,
  output [2:0] PC_Controller
);

  wire and_1_out, and_2_out, and_3_out, and_4_out, and_5_out, and_6_out, and_7_out, and_8_out, or_1_out,
       or_3_out, or_4_out, or_5_out, or_6_out;

  or or_1 (or_1_out, and_1_out, and_2_out);
  and and_1 (and_1_out, ~Zero_2, BNE);  // AND_Gate
  and and_2 (and_2_out, Zero_2, BEQ);
  and and_3 (and_3_out, ALUOUT_2[0], BGT);
  or or_2 (PC_Controller[0], or_1_out, or_3_out, or_4_out, or_5_out);
  or or_3 (or_3_out, and_3_out, and_4_out);
  and and_4 (and_4_out, ALUOUT_2[0], BLT);
  and and_5 (and_5_out, ALUOUT[0], BGTZ);
  or or_4 (or_4_out, and_5_out, and_6_out);
  and and_6 (and_6_out, ALUOUT[0], BLTZ);
  and and_7 (and_7_out, or_6_out, BGEZ);
  or or_5 (or_5_out, and_7_out, and_8_out);
  and and_8 (and_8_out, or_6_out, BLEZ);
  or or_6 (or_6_out, Zero, ALUOUT_3[0]);

  assign PC_Controller[2:1] = {JR, Jump};
endmodule

module ALU_Control (
  input  [4:0] ALUOp,
  input  [2:0] Func,
  input  [3:0] OP,
  input  R_Type,
  output JR,
  output [1:0] MemToReg,
  output [7:0] ALUCntrl
);

  wire AND_out, JR_out, OR_out, priority_encoder_1_p3, priority_encoder_1_p4, priority_encoder_1_p5,
       priority_encoder_1_p7, priority_encoder_1_p8, priority_encoder_1_p9, priority_encoder_2_p2,
       priority_encoder_2_p3, priority_encoder_2_p4, priority_encoder_2_p8, SLL_out, SRA_out, SRL_out,
       SUB_out;
  wire [4:0] multiplexer_1_out;

  Multiplexer #(.width(5)) multiplexer_1 (
    .in0(ALUOp), .in1({OP[1:0], Func}), .out(multiplexer_1_out), .sel(R_Type));  // open: en
  and AND (AND_out, ~multiplexer_1_out[4], ~multiplexer_1_out[3], ~multiplexer_1_out[2], ~multiplexer_1_out[1], ~multiplexer_1_out[0]);  // AND_Gate
  and OR (OR_out, ~multiplexer_1_out[4], ~multiplexer_1_out[3], ~multiplexer_1_out[1], multiplexer_1_out[0]);  // AND_Gate
  // Priority_Encoder #(.select(4)) priority_encoder_1: pin names not known; wires that end beside it: AND_out, OR_out, priority_encoder_1_p3, priority_encoder_1_p4, priority_encoder_1_p5, ALUCntrl[3:0], priority_encoder_1_p7, priority_encoder_1_p8, priority_encoder_1_p9
  and NOR (priority_encoder_1_p4, ~multiplexer_1_out[4], ~multiplexer_1_out[3], ~multiplexer_1_out[2], multiplexer_1_out[1], ~multiplexer_1_out[0]);  // AND_Gate
  and XOR (priority_encoder_1_p3, ~multiplexer_1_out[4], ~multiplexer_1_out[3], ~multiplexer_1_out[2], multiplexer_1_out[1], multiplexer_1_out[0]);  // AND_Gate
  and SLL (SLL_out, ~multiplexer_1_out[4], ~multiplexer_1_out[3], multiplexer_1_out[2], ~multiplexer_1_out[1], ~multiplexer_1_out[0]);  // AND_Gate
  and SRL (SRL_out, ~multiplexer_1_out[3], multiplexer_1_out[2], ~multiplexer_1_out[1], multiplexer_1_out[0]);  // AND_Gate
  and SRA (SRA_out, ~multiplexer_1_out[4], ~multiplexer_1_out[3], multiplexer_1_out[2], multiplexer_1_out[1], ~multiplexer_1_out[0]);  // AND_Gate
  // Priority_Encoder #(.select(4)) priority_encoder_2: pin names not known; wires that end beside it: 1'b1, priority_encoder_2_p2, priority_encoder_2_p3, priority_encoder_2_p4, SLL_out, SRL_out, SRA_out, priority_encoder_2_p8, ALUCntrl[7:4]
  and ROL (priority_encoder_2_p8, ~multiplexer_1_out[4], ~multiplexer_1_out[3], multiplexer_1_out[2], multiplexer_1_out[1], multiplexer_1_out[0]);  // AND_Gate
  and ADD (priority_encoder_1_p5, ~multiplexer_1_out[4], multiplexer_1_out[3], ~multiplexer_1_out[2], ~multiplexer_1_out[1], ~multiplexer_1_out[0]);  // AND_Gate
  or or_2 (priority_encoder_1_p7, SUB_out, priority_encoder_2_p3, priority_encoder_2_p2, priority_encoder_2_p4);
  and SUB (SUB_out, ~multiplexer_1_out[4], multiplexer_1_out[3], ~multiplexer_1_out[2], ~multiplexer_1_out[1], multiplexer_1_out[0]);  // AND_Gate
  and SLT (priority_encoder_1_p8, ~multiplexer_1_out[4], multiplexer_1_out[3], ~multiplexer_1_out[2], multiplexer_1_out[1], ~multiplexer_1_out[0]);  // AND_Gate
  and SLTU (priority_encoder_1_p9, ~multiplexer_1_out[4], multiplexer_1_out[3], ~multiplexer_1_out[2], multiplexer_1_out[1], multiplexer_1_out[0]);  // AND_Gate
  and SLTE (priority_encoder_2_p2, ~multiplexer_1_out[4], multiplexer_1_out[3], multiplexer_1_out[2], ~multiplexer_1_out[1], ~multiplexer_1_out[0]);  // AND_Gate
  and SLTEU (priority_encoder_2_p3, ~multiplexer_1_out[4], multiplexer_1_out[3], multiplexer_1_out[2], ~multiplexer_1_out[1], multiplexer_1_out[0]);  // AND_Gate
  and JALR (MemToReg[1], ~multiplexer_1_out[4], multiplexer_1_out[3], multiplexer_1_out[2], multiplexer_1_out[1], multiplexer_1_out[0]);  // AND_Gate
  and u_JR (JR_out, ~multiplexer_1_out[4], multiplexer_1_out[3], multiplexer_1_out[2], multiplexer_1_out[1], ~multiplexer_1_out[0]);  // AND_Gate
  or or_3 (JR, JR_out, MemToReg[1]);
  and BGT (priority_encoder_2_p4, multiplexer_1_out[4], ~multiplexer_1_out[3], ~multiplexer_1_out[2], ~multiplexer_1_out[1], ~multiplexer_1_out[0]);  // AND_Gate

  assign MemToReg[0] = 1'b0;

  // Other names for the same wires on the sheet: _1[3:0] = ALUCntrl[3:0]; _2[3:0] = ALUCntrl[7:4]
endmodule

module Main_Control_Unit (
  input  [15:0] RD2,
  input  [3:0] OP,
  output Jump,
  output BEQ,
  output BNE,
  output BLT,
  output BGT,
  output BLTZ,
  output BLEZ,
  output BGTZ,
  output BGEZ,
  output RegWrite,
  output [1:0] RegDest,
  output ALUSrc,
  output ExtOp,
  output MemWrite,
  output MemRead,
  output [1:0] MemToReg,
  output R_Type,
  output [4:0] ALUOp
);

  wire Add_out, ADDI_out, ANDI_out, BGEZ_out, BGTZ_out, BLEZ_out, BLTZ_out, GT_out, J_out, LT_out, or_2_out,
       or_8_out, ORI_out, R_Type_2_out, R_Type_out, Sub_out;
  wire [1:1] JAL_out, LUI_out;

  and u_R_Type (R_Type_out, ~OP[3], ~OP[2], ~OP[1], ~OP[0]);  // AND_Gate
  or or_1 (R_Type, R_Type_out, R_Type_2_out);
  and R_Type_2 (R_Type_2_out, ~OP[3], ~OP[2], ~OP[1], OP[0]);  // AND_Gate
  and LW (MemRead, ~OP[3], ~OP[2], OP[1], ~OP[0]);  // AND_Gate
  and SW (MemWrite, ~OP[3], ~OP[2], OP[1], OP[0]);  // AND_Gate
  and ANDI (ANDI_out, ~OP[3], OP[2], OP[1], ~OP[0]);  // AND_Gate
  and ORI (ORI_out, ~OP[3], OP[2], OP[1], OP[0]);  // AND_Gate
  and ADDI (ADDI_out, OP[3], ~OP[2], ~OP[1], ~OP[0]);  // AND_Gate
  and u_BNE (BNE, ~OP[3], OP[2], ~OP[1], OP[0]);  // AND_Gate
  and u_BEQ (BEQ, ~OP[3], OP[2], ~OP[1], ~OP[0]);  // AND_Gate
  and u_BLT (BLT, OP[3], OP[2], ~OP[1], OP[0]);  // AND_Gate
  and u_BGT (BGT, OP[3], OP[2], OP[1], OP[0]);
  and u_BLTZ (BLTZ_out, OP[3], OP[2], ~OP[1], ~OP[0]);  // AND_Gate
  and and_1 (BLTZ, BLTZ_out, ~RD2[0]);  // AND_Gate
  and u_BLEZ (BLEZ_out, OP[3], OP[2], ~OP[1], ~OP[0]);  // AND_Gate
  and and_2 (BLEZ, BLEZ_out, RD2[0]);
  and u_BGTZ (BGTZ_out, OP[3], OP[2], OP[1], ~OP[0]);  // AND_Gate
  and u_BGEZ (BGEZ_out, OP[3], OP[2], OP[1], ~OP[0]);  // AND_Gate
  and and_3 (BGTZ, BGTZ_out, ~RD2[0]);  // AND_Gate
  and and_4 (BGEZ, BGEZ_out, RD2[0]);
  and J (J_out, OP[3], ~OP[2], ~OP[1], OP[0]);  // AND_Gate
  and JAL (JAL_out[1], OP[3], ~OP[2], OP[1], OP[0]);  // AND_Gate
  and LUI (LUI_out[1], OP[3], ~OP[2], OP[1], ~OP[0]);  // AND_Gate
  or or_2 (or_2_out, R_Type_out, R_Type_2_out);
  or or_3 (Jump, JAL_out[1], J_out);
  or or_4 (RegWrite, LUI_out[1], R_Type_out, R_Type_2_out, MemRead, ANDI_out, ORI_out, ADDI_out, JAL_out[1]);
  or or_5 (RegDest[0], LUI_out[1], or_2_out);
  or or_6 (RegDest[1], LUI_out[1], JAL_out[1]);
  nor nor_1 (ALUSrc, BGEZ, R_Type_out, R_Type_2_out, BEQ, BNE, BLEZ, BLT, BGT, BLTZ, BGTZ);
  nor nor_2 (ExtOp, ORI_out, ANDI_out);
  or Add (Add_out, MemRead, MemWrite, ADDI_out);
  or Sub (Sub_out, BEQ, BNE);
  assign MemToReg = {1'b0, MemRead} | {2{LUI_out[1]}} | {JAL_out[1], 1'b0};  // OR_Gate or_7, 2 bits wide
  or LT (LT_out, BLT, BLEZ, BLTZ);
  or GT (GT_out, BGT, BGEZ, BGTZ);
  or or_8 (or_8_out, 1'b1, ANDI_out);
  // Priority_Encoder #(.select(5)) priority_encoder_1: pin names not known; wires that end beside it: or_8_out, ORI_out, Add_out, Sub_out, LT_out, ALUOp, GT_out

  // Notes on the sheet:
  //   OR
  //   AND
endmodule
